# Fritzing sketch L293D sketch (saved by Fritzing 0.7.7b)
breadboards: 1

parts:
  Raspberry_Pi1 = Raspberry Pi (Model B)
  IC1 = L293D [package=THT]
  VCC1 = Battery
  M1 = DC Motor

nets:
  N1: Raspberry_Pi1.3V3, IC1.Enable_1, IC1.+V
  N2: Raspberry_Pi1.GND, IC1.0V, VCC1.-
  N3: Raspberry_Pi1.#18, IC1.In_1
  N4: Raspberry_Pi1.#23, IC1.In_2
  N5: IC1.Out_1_(_Controlled_by_Enable_1_), M1.pin_1
  N6: IC1.Out_2_(_Controlled_by_Enable_1_), M1.pin_2
  N7: IC1.+Vmotor, VCC1.+

notes:
  Power for the motor
  Vanilla DC motor

custom parts:
  Raspberry Pi (Model B): Raspberry Pi Single-board Computer, Model B
